# Fritzing sketch capstone (saved by Fritzing 1.0.0rc)
breadboards: 5

parts:
  Breadboard4 = Breadboard Split Power
  Breadboard5 = Breadboard Split Power
  A1 = Particle - Photon2
  Neopixel1 = Adafruit RBG Smart Neopixel [package="DIP (Dual Inline) [THT]"]
  Neopixel2 = Adafruit RBG Smart Neopixel [package="DIP (Dual Inline) [THT]"]
  Neopixel3 = Adafruit RBG Smart Neopixel [package="DIP (Dual Inline) [THT]"]
  Neopixel4 = Adafruit RBG Smart Neopixel [package="DIP (Dual Inline) [THT]"]
  S1 = Pushbutton [package="[THT]"]
  R2 = Resistor [tolerance=±5% resistance=220 package="2010 [SMD]"]
  D1 = LTE-302 [package=lte-302]
  R4 = Resistor [tolerance=±5% resistance=220 package="2010 [SMD]"]
  S3 = Pushbutton [package="[THT]"]
  U2 = SWITCH_SPDT [package=kps-1290]
  R5 = Resistor [tolerance=±5% resistance=220 package="2010 [SMD]"]
  OLED_I2C2 = OLED 128x64 I2C Monochrome Display
  Q1 = PNP-Transistor [package="TO92 [THT]"]
  R6 = Resistor [tolerance=±5% resistance=1.8 package="2010 [SMD]"]
  R7 = Resistor [tolerance=±5% resistance=3.3 package="2010 [SMD]"]
  Neopixel5 = Adafruit RBG Smart Neopixel [package="DIP (Dual Inline) [THT]"]
  Neopixel6 = Adafruit RBG Smart Neopixel [package="DIP (Dual Inline) [THT]"]
  Neopixel7 = Adafruit RBG Smart Neopixel [package="DIP (Dual Inline) [THT]"]
  Neopixel8 = Adafruit RBG Smart Neopixel [package="DIP (Dual Inline) [THT]"]
  Neopixel9 = Adafruit RBG Smart Neopixel [package="DIP (Dual Inline) [THT]"]
  Neopixel10 = Adafruit RBG Smart Neopixel [package="DIP (Dual Inline) [THT]"]

nets (from the breadboard view):
  N1: Breadboard4.pin3Y, Breadboard4.pin15Y, Breadboard4.pin17Y, Breadboard4.pin21Y, Breadboard4.pin29Y, Breadboard5.pin3Y, Breadboard5.pin15Y, Breadboard5.pin17Y, Breadboard5.pin29Y, A1.Pin_2, D1.A
  N2: Breadboard4.pin4Z, Breadboard4.pin20Z, Breadboard4.pin29Z, Breadboard5.pin3Z, Breadboard5.pin11Z, A1.Pin_4, A1.Pin_23, A1.Pin_26, A1.Pin_30, A1.Pin_35, A1.Pin_37, Neopixel1.G, Neopixel2.G, Neopixel3.G, Neopixel4.+, Neopixel4.G, S1.Pin_1, S1.Pin_2, R2.Pin_1, R4.Pin_1, S3.Pin_1, S3.Pin_2, U2.P, R5.Pin_1, Q1.C, R6.Pin_0, Neopixel5.+, Neopixel5.G, Neopixel5.In, Neopixel6.+, Neopixel6.G, Neopixel6.In, Neopixel7.+, Neopixel7.G, Neopixel7.In, Neopixel8.+, Neopixel8.G, Neopixel9.+, Neopixel9.G, Neopixel10.+, Neopixel10.G
  N3: A1.Pin_17, OLED_I2C2.SCK
  N4: A1.Pin_19, R7.Pin_0
  N5: Neopixel1.O, Neopixel2.In
  N6: Neopixel2.O, Neopixel3.In
  N7: Neopixel3.O, Neopixel4.In
  N8: S1.Pin_3, S1.Pin_4, R2.Pin_0, S3.Pin_3, S3.Pin_4, U2.S, OLED_I2C2.GND
  N9: D1.C, R4.Pin_0
  N10: U2.O, R5.Pin_0, OLED_I2C2.VDD
  N11: Q1.E, R6.Pin_1
  N12: Q1.B, R7.Pin_1
  N13: Neopixel8.In, Neopixel8.O, Neopixel9.In, Neopixel9.O, Neopixel10.In, Neopixel10.O

custom parts:
  Breadboard Split Power: A custom 6 pin per group power supply strip where the top row (ground) is all bussed together and the bottom row (+V) is split in two groups of 12 pins. This version is modified to be a loadable part and was rescaled to be on the standard 1px = 1thou grid with the size set in inches
  Particle - Photon2: The Photon 2 is a microcontroller and Wi-Fi networking developed by particle. Features: 802.11a/b/g/n Wi-Fi, 2.4 GHz and 5 GHz Integrated PCB antenna Integrated U.FL connector for external antenna Integrated RF switch BLE 5 using same antenna as Wi-Fi Realtek RTL8721DM MCU ARM Cortex M33 CPU, 200 MHz 2048 KB (2 MB) user application maximum size 3072 KB (3 MB) of RAM available to user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
  Pushbutton: A generic pushbutton.
